// Logisim project 74x138.circ as structural Verilog: 1 circuit, main circuit 74x138
module _74x138 (
  input  G1,
  input  G2A_L,
  input  G2B_L,
  input  A,
  input  B,
  input  C,
  output Y0_L,
  output Y1_L,
  output Y2_L,
  output Y3_L,
  output Y4_L,
  output Y5_L,
  output Y6_L,
  output Y7_L
);

  wire nor_1_out, not_1_out, not_2_out, not_3_out, not_4_out, not_5_out, not_6_out, not_7_out;

  not not_1 (not_1_out, G1);
  not not_2 (not_2_out, A);
  not not_3 (not_3_out, B);
  not not_4 (not_4_out, C);
  nor nor_1 (nor_1_out, not_1_out, G2A_L, G2B_L);
  not not_5 (not_5_out, not_2_out);
  not not_6 (not_6_out, not_3_out);
  not not_7 (not_7_out, not_4_out);
  nand nand_1 (Y0_L, not_2_out, not_3_out, not_4_out, nor_1_out);
  nand nand_2 (Y1_L, nor_1_out, not_4_out, not_3_out, not_5_out);
  nand nand_3 (Y2_L, nor_1_out, not_4_out, not_4_out, not_2_out, not_6_out);
  nand nand_4 (Y3_L, nor_1_out, not_4_out, not_6_out, not_5_out);
  nand nand_5 (Y4_L, nor_1_out, not_2_out, not_3_out, not_7_out);
  nand nand_6 (Y5_L, nor_1_out, not_3_out, not_5_out, not_7_out);
  nand nand_7 (Y6_L, nor_1_out, not_2_out, not_6_out, not_7_out);
  nand nand_8 (Y7_L, nor_1_out, not_5_out, not_6_out, not_7_out);
endmodule
