// Logisim project 74x280.circ as structural Verilog: 1 circuit, main circuit 74x280
module _74x280 (
  input  A,
  input  B,
  input  C,
  input  D,
  input  E,
  input  F,
  input  G,
  input  H,
  input  I,
  output EVEN,
  output ODD
);

  wire not_1_out, xor_1_out, xor_2_out, xor_3_out, xor_4_out, xor_5_out, xor_6_out, xor_7_out, xor_8_out;

  xor xor_1 (xor_1_out, A, B);
  xor xor_2 (xor_2_out, D, E);
  xor xor_3 (xor_3_out, G, H);
  xor xor_4 (xor_4_out, xor_1_out, C);
  xor xor_5 (xor_5_out, xor_2_out, F);
  xor xor_6 (xor_6_out, xor_3_out, I);
  not not_1 (not_1_out, xor_6_out);
  xor xor_7 (xor_7_out, xor_4_out, xor_5_out);
  xor xor_8 (xor_8_out, xor_4_out, xor_5_out);
  xor xor_9 (EVEN, xor_7_out, not_1_out);
  xor xor_10 (ODD, xor_8_out, xor_6_out);
endmodule
