// Logisim project Question3.circ as structural Verilog: 1 circuit, main circuit main
module main (
  input  A,
  input  B,
  input  C,
  input  D,
  output Y
);

  wire not_1_out, xor_1_out, xor_2_out;

  xor xor_1 (xor_1_out, A, B);
  xor xor_2 (xor_2_out, xor_1_out, C);
  not not_1 (not_1_out, xor_2_out);
  nand nand_1 (Y, not_1_out, D);
endmodule
