// Logisim project Question4.circ as structural Verilog: 1 circuit, main circuit main
module main (
  input  DU7,
  input  DU5,
  input  DU3,
  input  DU1,
  input  DU6,
  input  DU2,
  input  DU4,
  output NOERROR_L,
  output DC_L1,
  output DC_L2,
  output DC_L3,
  output DC_L4,
  output DC_L5,
  output DC_L6,
  output DC_L7
);

  wire _74x138_y0_l, _74x138_y1_l, _74x138_y2_l, _74x138_y3_l, _74x138_y4_l, _74x138_y5_l, _74x138_y6_l,
       _74x138_y7_l, _74x208_odd, _74x280_2_odd, _74x280_odd, not_2_out, not_3_out, not_4_out, not_5_out,
       not_6_out, not_7_out, not_8_out, not_9_out, not_10_out, not_11_out, not_12_out, not_13_out,
       not_14_out, not_15_out;

  _74x280 _74x208 (
    .A(DU7), .B(DU5), .C(DU3), .D(DU1), .E(1'b0), .F(1'b0), .G(1'b0), .H(1'b0), .I(1'b0), .ODD(_74x208_odd));  // open: EVEN
  _74x280 _74x280 (
    .A(DU7), .B(DU6), .C(DU3), .D(DU2), .E(1'b0), .F(1'b0), .G(1'b0), .H(1'b0), .I(1'b0), .ODD(_74x280_odd));  // open: EVEN
  _74x280 _74x280_2 (
    .A(DU7), .B(DU6), .C(DU5), .D(DU4), .E(1'b0), .F(1'b0), .G(1'b0), .H(1'b0), .I(1'b0), .ODD(_74x280_2_odd));  // open: EVEN
  _74x138 _74x138 (
    .G1(1'b1), .G2A_L(1'b0), .G2B_L(1'b0), .A(_74x208_odd), .B(_74x280_odd), .C(_74x280_2_odd),
    .Y0_L(_74x138_y0_l), .Y1_L(_74x138_y1_l), .Y2_L(_74x138_y2_l), .Y3_L(_74x138_y3_l), .Y4_L(_74x138_y4_l),
    .Y5_L(_74x138_y5_l), .Y6_L(_74x138_y6_l), .Y7_L(_74x138_y7_l));
  not not_1 (NOERROR_L, _74x138_y0_l);
  not not_2 (not_2_out, _74x138_y1_l);
  not not_3 (not_3_out, not_2_out);
  not not_4 (not_4_out, not_5_out);
  not not_5 (not_5_out, _74x138_y2_l);
  not not_6 (not_6_out, not_7_out);
  not not_7 (not_7_out, _74x138_y3_l);
  not not_8 (not_8_out, not_9_out);
  not not_9 (not_9_out, _74x138_y4_l);
  not not_10 (not_10_out, _74x138_y5_l);
  not not_11 (not_11_out, not_10_out);
  not not_12 (not_12_out, not_13_out);
  not not_13 (not_13_out, _74x138_y6_l);
  not not_14 (not_14_out, not_15_out);
  not not_15 (not_15_out, _74x138_y7_l);
  xnor xnor_1 (DC_L1, DU1, not_3_out);
  xnor xnor_2 (DC_L2, DU2, not_4_out);
  xnor xnor_3 (DC_L3, DU3, not_6_out);
  xnor xnor_4 (DC_L4, DU4, not_8_out);
  xnor xnor_5 (DC_L5, DU5, not_11_out);
  xnor xnor_6 (DC_L6, DU6, not_12_out);
  xnor xnor_7 (DC_L7, DU7, not_14_out);
endmodule
