// Logisim project Question5.circ as structural Verilog: 1 circuit, main circuit main
module main (
  input  G1,
  input  G2,
  input  G3,
  input  T1,
  input  T2,
  output Y1,
  output Y2,
  output Y3
);

  wire and_1_out, and_2_out, and_3_out, and_4_out, and_5_out, and_6_out, and_7_out, and_8_out, and_9_out,
       and_10_out, and_11_out, and_12_out, not_1_out, not_2_out, not_3_out, not_4_out, not_5_out, not_6_out,
       not_7_out, not_8_out, not_9_out, not_10_out, not_11_out;

  not not_1 (not_1_out, T1);
  not not_2 (not_2_out, T2);
  and and_1 (and_1_out, not_1_out, not_2_out);
  and and_2 (and_2_out, not_1_out, T2);
  and and_3 (and_3_out, not_2_out, T1);
  not not_3 (not_3_out, G2);
  not not_4 (not_4_out, G1);
  not not_5 (not_5_out, G1);
  not not_6 (not_6_out, G2);
  not not_7 (not_7_out, G2);
  not not_8 (not_8_out, G1);
  not not_9 (not_9_out, G3);
  not not_10 (not_10_out, G3);
  not not_11 (not_11_out, G2);
  and and_4 (and_4_out, and_1_out, and_1_out, not_3_out, G3, not_4_out);
  and and_5 (and_5_out, and_1_out, G2, not_5_out);
  and and_6 (and_6_out, and_1_out, G1);
  and and_7 (and_7_out, and_2_out, G2);
  and and_8 (and_8_out, and_2_out, not_6_out, G1);
  and and_9 (and_9_out, and_2_out, not_7_out, not_8_out, G3);
  and and_10 (and_10_out, G3, and_3_out);
  and and_11 (and_11_out, not_9_out, G2, and_3_out);
  and and_12 (and_12_out, not_10_out, G1, not_11_out, and_3_out);
  or or_1 (Y1, and_6_out, and_12_out, and_8_out);
  or or_2 (Y2, and_5_out, and_7_out, and_11_out);
  or or_3 (Y3, and_4_out, and_9_out, and_10_out);
endmodule
