// Logisim project D锁存器.circ as structural Verilog: 1 circuit, main circuit main
module main (
  input  D,
  input  C,
  output Q,
  output QN
);

  wire nand_1_out, nand_2_out, not_1_out;

  not not_1 (not_1_out, D);
  nand nand_1 (nand_1_out, D, C);
  nand nand_2 (nand_2_out, not_1_out, C);
  nand nand_3 (Q, nand_1_out, QN);
  nand nand_4 (QN, Q, nand_2_out);
endmodule
