// Logisim project 用D触发器构造JK触发器和T触发器.circ as structural Verilog: 1 circuit, main circuit main
module main (
  input  J,
  input  K,
  input  T,
  output Q,
  output QN,
  output Q_2,
  output QN_2
);

  wire and_1_out, and_2_out, clock_1_out, clock_2_out, not_1_out, or_1_out, xor_1_out;

  Clock clock_1 (.out(clock_1_out));
  Clock clock_2 (.out(clock_2_out));
  and and_1 (and_1_out, QN, J);
  not not_1 (not_1_out, K);
  and and_2 (and_2_out, not_1_out, Q);
  or or_1 (or_1_out, and_1_out, and_2_out);
  xor xor_1 (xor_1_out, T, Q_2);
  D_Flip_Flop d_ff_1 (.clk(clock_1_out), .D(or_1_out), .Q(Q), .Qn(QN), .preset(1'b0), .en(1'b1), .reset(1'b0));
  D_Flip_Flop d_ff_2 (.clk(clock_2_out), .D(xor_1_out), .Q(Q_2), .Qn(QN_2), .preset(1'b0), .en(1'b1), .reset(1'b0));

  // Notes on the sheet:
  //   CLK
  //   CLK
  //   用D触发器构造JK触发器
  //   用D触发器构造T触发器
endmodule
