// Logisim project 用JK触发器构造D触发器和T触发器.circ as structural Verilog: 1 circuit, main circuit main
module main (
  input  D,
  input  T,
  output Q,
  output QN,
  output Q_2,
  output QN_2
);

  wire clock_1_out, clock_2_out, not_1_out;

  Clock clock_1 (.out(clock_1_out));
  not not_1 (not_1_out, D);
  Clock clock_2 (.out(clock_2_out));
  J_K_Flip_Flop j_k_ff_1 (
    .J(D), .clk(clock_1_out), .K(not_1_out), .Q(Q), .Qn(QN), .preset(1'b0), .en(1'b1), .reset(1'b0));
  J_K_Flip_Flop j_k_ff_2 (.J(T), .clk(clock_2_out), .K(T), .Q(Q_2), .Qn(QN_2), .preset(1'b0), .en(1'b1), .reset(1'b0));

  // Notes on the sheet:
  //   CLK
  //   CLK
  //   用JK触发器构造D触发器
  //   用JK触发器构造T触发器
endmodule
