// Logisim project 用T触发器构造D触发器和JK触发器.circ as structural Verilog: 1 circuit, main circuit main
module main (
  input  D,
  input  J,
  input  K,
  output Q,
  output QN,
  output Q_2,
  output QN_2
);

  wire and_1_out, and_2_out, clock_1_out, clock_2_out, not_1_out, or_1_out, xor_1_out, xor_2_out;

  Clock clock_1 (.out(clock_1_out));
  Clock clock_2 (.out(clock_2_out));
  and and_1 (and_1_out, QN_2, J);
  not not_1 (not_1_out, K);
  and and_2 (and_2_out, not_1_out, Q_2);
  xor xor_1 (xor_1_out, D, Q);
  or or_1 (or_1_out, and_1_out, and_2_out);
  T_Flip_Flop t_ff_1 (.clk(clock_1_out), .T(xor_1_out), .Q(Q), .Qn(QN), .preset(1'b0), .reset(1'b0), .en(1'b1));
  xor xor_2 (xor_2_out, or_1_out, Q_2);
  T_Flip_Flop t_ff_2 (.clk(clock_2_out), .T(xor_2_out), .Q(Q_2), .Qn(QN_2), .preset(1'b0), .reset(1'b0), .en(1'b1));

  // Notes on the sheet:
  //   CLK
  //   CLK
  //   用T触发器构造D触发器
  //   用T触发器构造JK触发器
endmodule
