// Logisim project 问题1主从式D触发器.circ as structural Verilog: 1 circuit, main circuit main
module main (
  input  D,
  input  CLK,
  output Q,
  output QN
);

  wire \D锁存器_q , not_1_out, not_2_out;

  not not_1 (not_1_out, CLK);
  \D锁存器_main  \D锁存器  (.D(D), .C(not_1_out), .Q(\D锁存器_q ));  // open: QN
  not not_2 (not_2_out, not_1_out);
  \D锁存器_main  main_1 (.D(\D锁存器_q ), .C(not_2_out), .Q(Q), .QN(QN));

  // Notes on the sheet:
  //   D锁存器
endmodule
