// Logisim project 问题2.circ as structural Verilog: 1 circuit, main circuit main
module main (
  input  R,
  input  in_2,
  input  in_3,
  output out_4
);

  wire clock_1_out, d_ff_1_q, d_ff_1_qn, d_ff_2_q, d_ff_2_qn, d_ff_3_q, d_ff_3_qn, nand_1_out, nand_2_out,
       nand_3_out, nand_4_out, nand_5_out, nand_6_out, nand_7_out, nand_8_out, nand_9_out, nor_1_out,
       nor_2_out, nor_3_out, not_1_out, not_2_out, not_3_out, not_4_out, not_5_out, xor_1_out;

  Clock clock_1 (.out(clock_1_out));
  not not_1 (not_1_out, R);
  nand nand_1 (nand_1_out, in_2, clock_1_out);
  nand nand_2 (nand_2_out, not_1_out, d_ff_2_q, d_ff_3_q);
  xor xor_1 (xor_1_out, R, d_ff_3_q);
  not not_2 (not_2_out, xor_1_out);
  nand nand_3 (nand_3_out, not_1_out, d_ff_1_qn, d_ff_2_qn, d_ff_3_q);
  not not_3 (not_3_out, nand_3_out);
  nand nand_4 (nand_4_out, R, d_ff_1_q, d_ff_3_qn);
  nand nand_5 (nand_5_out, d_ff_1_q, not_2_out);
  nor nor_1 (nor_1_out, nor_3_out, not_3_out);
  nand nand_6 (nand_6_out, nand_2_out, nor_2_out);
  nor nor_2 (nor_2_out, not_5_out, not_4_out);
  not not_4 (not_4_out, nand_5_out);
  nor nor_3 (nor_3_out, d_ff_2_qn, xor_1_out);
  nand nand_7 (nand_7_out, nor_1_out, nand_4_out);
  D_Flip_Flop d_ff_1 (
    .clk(nand_1_out), .D(nand_6_out), .Q(d_ff_1_q), .Qn(d_ff_1_qn), .preset(1'b0), .en(1'b1), .reset(in_3));
  D_Flip_Flop d_ff_2 (
    .clk(nand_1_out), .D(nand_7_out), .Q(d_ff_2_q), .Qn(d_ff_2_qn), .preset(1'b0), .en(1'b1), .reset(in_3));
  D_Flip_Flop d_ff_3 (
    .clk(nand_1_out), .D(d_ff_3_qn), .Q(d_ff_3_q), .Qn(d_ff_3_qn), .preset(1'b0), .en(1'b1), .reset(in_3));
  nand nand_8 (nand_8_out, R, d_ff_1_qn, d_ff_2_qn, d_ff_3_qn);
  nand nand_9 (nand_9_out, d_ff_1_q, not_1_out, d_ff_2_qn, d_ff_3_q);
  not not_5 (not_5_out, nand_8_out);
  nand nand_10 (out_4, nand_8_out, nand_9_out);
endmodule
