// Logisim project 问题3.circ as structural Verilog: 1 circuit, main circuit main
module main (
  input  Cin,
  output Y
);

  wire and_1_out, and_2_out, clock_1_out, d_ff_1_q, d_ff_1_qn, not_1_out, or_1_out, or_2_out, Q1_q, Q1_qn;

  Clock clock_1 (.out(clock_1_out));
  not not_1 (not_1_out, Cin);
  and and_1 (and_1_out, not_1_out, Q1_q, d_ff_1_q);
  or or_1 (or_1_out, Cin, and_1_out);
  and and_2 (and_2_out, not_1_out, Q1_q, d_ff_1_qn);
  or or_2 (or_2_out, Cin, and_2_out);
  D_Flip_Flop Q1 (.clk(clock_1_out), .D(or_1_out), .Q(Q1_q), .Qn(Q1_qn), .preset(1'b0), .en(1'b1), .reset(1'b0));
  D_Flip_Flop d_ff_1 (
    .clk(clock_1_out), .D(or_2_out), .Q(d_ff_1_q), .Qn(d_ff_1_qn), .preset(1'b0), .en(1'b1), .reset(1'b0));
  and and_3 (Y, Q1_qn, Cin, d_ff_1_q);

  // Notes on the sheet:
  //   CLK
  //   Q0
endmodule
