// Logisim project 问题4.circ as structural Verilog: 1 circuit, main circuit main
module main (
  input  in_1,
  input  in_2,
  input  in_3,
  input  in_4,
  input  in_5,
  input  in_6,
  input  in_7,
  input  in_8,
  output out_9,
  output out_10,
  output out_11,
  output out_12
);

  wire and_1_out, and_2_out, and_3_out, and_4_out, clock_1_out, d_ff_1_qn, d_ff_2_qn, d_ff_3_qn, d_ff_4_qn;

  Clock clock_1 (.out(clock_1_out));
  and and_1 (and_1_out, d_ff_1_qn, d_ff_2_qn, d_ff_3_qn);
  and and_2 (and_2_out, out_9, d_ff_2_qn, d_ff_3_qn, d_ff_4_qn);
  and and_3 (and_3_out, d_ff_1_qn, out_10, d_ff_3_qn, d_ff_4_qn);
  and and_4 (and_4_out, d_ff_1_qn, d_ff_2_qn, out_11, d_ff_4_qn);
  D_Flip_Flop d_ff_1 (
    .clk(clock_1_out), .D(and_1_out), .Q(out_9), .Qn(d_ff_1_qn), .preset(in_1), .en(1'b1), .reset(in_2));
  D_Flip_Flop d_ff_2 (
    .clk(clock_1_out), .D(and_2_out), .Q(out_10), .Qn(d_ff_2_qn), .preset(in_3), .en(1'b1), .reset(in_4));
  D_Flip_Flop d_ff_3 (
    .clk(clock_1_out), .D(and_3_out), .Q(out_11), .Qn(d_ff_3_qn), .preset(in_5), .en(1'b1), .reset(in_6));
  D_Flip_Flop d_ff_4 (
    .clk(clock_1_out), .D(and_4_out), .Q(out_12), .Qn(d_ff_4_qn), .preset(in_7), .en(1'b1), .reset(in_8));
endmodule
