// Logisim project 74x194.circ as structural Verilog: 1 circuit, main circuit main
module main (
  input  CLK,
  input  CLR_L,
  input  S1,
  input  S0,
  input  LIN,
  input  D,
  input  C,
  input  B,
  input  A,
  input  RIN,
  output QD,
  output QC,
  output QB,
  output QA
);

  wire and_1_out, and_2_out, and_3_out, and_4_out, and_5_out, and_6_out, and_7_out, and_8_out, and_9_out,
       and_10_out, and_11_out, and_12_out, and_13_out, and_14_out, and_15_out, and_16_out, not_1_out,
       not_2_out, not_3_out, or_1_out, or_2_out, or_3_out, or_4_out;

  not not_1 (not_1_out, CLR_L);
  not not_2 (not_2_out, S1);
  not not_3 (not_3_out, S0);
  and and_1 (and_1_out, S1, not_3_out, LIN);
  and and_2 (and_2_out, not_2_out, not_3_out, QD);
  and and_3 (and_3_out, S1, S0, D);
  and and_4 (and_4_out, not_2_out, S0, QC);
  and and_5 (and_5_out, S1, not_3_out, QC);
  and and_6 (and_6_out, not_2_out, not_2_out, not_3_out, QB);
  and and_7 (and_7_out, S1, S0, B);
  and and_8 (and_8_out, S0, not_2_out, QA);
  or or_1 (or_1_out, and_1_out, and_2_out, and_3_out, and_4_out);
  or or_2 (or_2_out, and_5_out, and_6_out, and_7_out, and_8_out);
  and and_9 (and_9_out, S1, not_3_out, QD);
  and and_10 (and_10_out, not_2_out, not_3_out, QC);
  and and_11 (and_11_out, S1, S0, C);
  and and_12 (and_12_out, not_2_out, S0, QB);
  and and_13 (and_13_out, not_3_out, S1, QB);
  and and_14 (and_14_out, not_3_out, not_2_out, QA);
  and and_15 (and_15_out, S0, S1, A);
  and and_16 (and_16_out, S0, not_2_out, RIN);
  or or_3 (or_3_out, and_9_out, and_10_out, and_12_out, and_11_out);
  or or_4 (or_4_out, and_14_out, and_15_out, and_16_out, and_13_out);
  D_Flip_Flop d_ff_1 (.clk(CLK), .D(or_1_out), .Q(QD), .preset(1'b0), .en(1'b1), .reset(not_1_out));  // open: Qn
  D_Flip_Flop d_ff_2 (.clk(CLK), .D(or_3_out), .Q(QC), .preset(1'b0), .en(1'b1), .reset(not_1_out));  // open: Qn
  D_Flip_Flop d_ff_3 (.clk(CLK), .D(or_2_out), .Q(QB), .preset(1'b0), .en(1'b1), .reset(not_1_out));  // open: Qn
  D_Flip_Flop d_ff_4 (.clk(CLK), .D(or_4_out), .Q(QA), .preset(1'b0), .en(1'b1), .reset(not_1_out));  // open: Qn
endmodule
