// Logisim project question1.circ as structural Verilog: 1 circuit, main circuit main
module main (
  output QA,
  output QB,
  output QC,
  output QD,
  output QA_2,
  output QB_2,
  output QC_2,
  output QD_2
);

  wire clock_1_out, clock_2_out, nand_1_out, nand_2_out;

  Clock clock_1 (.out(clock_1_out));
  Clock clock_2 (.out(clock_2_out));
  _74161 u_74161_1 (
    .A(1'b0), .B(1'b0), .C(1'b0), .D(1'b0), .ENT(1'b1), .ENP(1'b1), .LD_L(1'b1), .CLR_L(nand_1_out),
    .CLK(clock_2_out), .QA(QA), .QB(QB), .QC(QC), .QD(QD));  // open: RCO
  _74163 u_74163_1 (
    .A(1'b1), .B(1'b1), .C(1'b0), .D(1'b0), .ENT(1'b1), .ENP(1'b1), .LD_L(nand_2_out), .CLR_L(1'b1),
    .QA(QA_2), .QB(QB_2), .QC(QC_2), .QD(QD_2), .CLK(clock_1_out));  // open: RCO
  nand nand_1 (nand_1_out, QD, QC);
  nand nand_2 (nand_2_out, QD_2, QC_2, QB_2);

  // Notes on the sheet:
  //   CLK
  //   74HC161
  //   74HC163
  //   74HC00
  //   74HC10
endmodule
