// Logisim project question2.circ as structural Verilog: 1 circuit, main circuit main
module main (
  output QD,
  output QD_2,
  output QD_3,
  output QC,
  output QC_2,
  output QC_3,
  output QB,
  output QB_2,
  output QB_3,
  output QA,
  output QA_2,
  output QA_3
);

  wire clock_1_out, n74163_2_rco, nand_1_out, nand_2_out, nand_3_out, nand_4_out, not_1_out, not_2_out,
       not_3_out, not_4_out;

  Clock clock_1 (.out(clock_1_out));
  _74163 u_74163_1 (
    .A(1'b0), .B(1'b0), .C(1'b0), .D(1'b0), .ENT(1'b1), .ENP(1'b1), .LD_L(1'b1), .CLR_L(not_2_out), .QA(QA),
    .QB(QB), .QC(QC), .QD(QD), .CLK(clock_1_out));  // open: RCO
  _74163 u_74163_2 (
    .A(1'b0), .B(1'b0), .C(1'b0), .D(1'b0), .ENT(not_1_out), .ENP(not_1_out), .LD_L(1'b1), .CLR_L(not_4_out),
    .QA(QA_2), .QB(QB_2), .QC(QC_2), .QD(QD_2), .RCO(n74163_2_rco), .CLK(clock_1_out));
  nand nand_1 (nand_1_out, QD, QA);
  not not_1 (not_1_out, nand_1_out);
  not not_2 (not_2_out, nand_2_out);
  nand nand_2 (nand_2_out, nand_1_out, nand_1_out, nand_1_out, nand_1_out);
  _74163 u_74163_3 (
    .A(1'b0), .B(1'b0), .C(1'b0), .D(1'b0), .ENT(not_3_out), .ENP(not_3_out), .LD_L(1'b1),
    .CLR_L(nand_1_out), .QA(QA_3), .QB(QB_3), .QC(QC_3), .QD(QD_3), .CLK(clock_1_out));  // open: RCO
  nand nand_3 (nand_3_out, QA_2, QD_2, QD, QA);
  not not_3 (not_3_out, nand_3_out);
  nand nand_4 (nand_4_out, nand_1_out, nand_3_out);
  nand nand_5 (nand_1_out, QA_3, QB_2, QC, QC_3);
  not not_4 (not_4_out, nand_4_out);

  // Notes on the sheet:
  //   74HC00
  //   74HC04
  //   74HC00
  //   74HC20
  //   74HC04
  //   74HC04
  //   74HC00
  //   74HC20
  //   20
endmodule
