// Logisim project question3.circ as structural Verilog: 1 circuit, main circuit main
module main (
  output QD,
  output QC,
  output QB,
  output QA
);

  wire clock_1_out, nor_1_out, nor_2_out, nor_3_out, xor_1_out, xor_2_out;

  Clock clock_1 (.out(clock_1_out));
  _74x194_main main_1 (
    .CLK(clock_1_out), .CLR_L(1'b1), .S1(1'b1), .S0(1'b0), .LIN(xor_2_out), .D(1'b0), .C(1'b0), .B(1'b0),
    .A(1'b0), .RIN(1'b0), .QD(QD), .QC(QC), .QB(QB), .QA(QA));
  nor nor_1 (nor_1_out, QC, QB);
  xor xor_1 (xor_1_out, QA, QB);
  not nor_2 (nor_2_out, nor_1_out);  // NOR_Gate
  nor nor_3 (nor_3_out, nor_2_out, QD);
  xor xor_2 (xor_2_out, nor_3_out, xor_1_out);

  // Notes on the sheet:
  //   74HC86
  //   74HC02
  //   74HC02
  //   74HC02
  //   74HC86
endmodule
