// Logisim project question4.circ as structural Verilog: 1 circuit, main circuit main
module main (
  input  S0,
  output out_2,
  output out_3,
  output out_4,
  output out_5,
  output out_6,
  output out_7,
  output out_8,
  output out_9,
  output out_10,
  output out_11
);

  wire _74HC00_2_out, _74HC00_3_out, _74HC00_4_out, _74HC00_5_out, _74HC00_6_out, _74HC00_out, _74HC10_2_out,
       _74HC10_out, clock_1_out, not_1_out, not_2_out, not_3_out, not_4_out, not_5_out, not_6_out, not_7_out,
       not_8_out;

  Clock clock_1 (.out(clock_1_out));
  _74x194_main main_1 (
    .CLK(clock_1_out), .CLR_L(1'b1), .S1(1'b1), .S0(S0), .LIN(out_6), .D(1'b0), .C(1'b0), .B(1'b0), .A(1'b1),
    .RIN(1'b1), .QD(out_5), .QC(out_4), .QB(out_3), .QA(out_2));
  not not_1 (not_1_out, out_2);
  not not_2 (not_2_out, out_3);
  nand _74HC00 (_74HC00_out, not_3_out, out_5);
  nand _74HC00_2 (_74HC00_2_out, not_1_out, out_5);
  not not_3 (not_3_out, out_4);
  not not_4 (not_4_out, out_5);
  nand _74HC00_3 (_74HC00_3_out, not_3_out, not_2_out);
  nand _74HC20 (out_6, _74HC00_out, _74HC00_2_out, _74HC00_3_out, _74HC10_out);
  nand _74HC10 (_74HC10_out, not_4_out, out_4, out_2);
  _74x194_main main_2 (
    .CLK(clock_1_out), .CLR_L(1'b1), .S1(1'b1), .S0(S0), .LIN(out_11), .D(1'b0), .C(1'b1), .B(1'b1),
    .A(1'b1), .RIN(1'b1), .QD(out_10), .QC(out_9), .QB(out_8), .QA(out_7));
  not not_5 (not_5_out, out_7);
  nand _74HC00_4 (_74HC00_4_out, not_6_out, not_6_out, out_10);
  not not_6 (not_6_out, out_9);
  not not_7 (not_7_out, out_8);
  nand _74HC00_5 (_74HC00_5_out, not_5_out, out_10);
  nand _74HC00_6 (_74HC00_6_out, not_7_out, not_6_out);
  nand _74HC20_2 (out_11, _74HC00_4_out, _74HC00_5_out, _74HC00_6_out, _74HC10_2_out);
  not not_8 (not_8_out, out_10);
  nand _74HC10_2 (_74HC10_2_out, not_8_out, out_9, out_7);

  // Notes on the sheet:
  //   74LS194
  //   74LS194
endmodule
