// Logisim project 并行串行转换原理图.circ as structural Verilog: 1 circuit, main circuit main
module main (
  input  \串入 ,
  input  _7,
  input  _6,
  input  \串入_2 ,
  input  _5,
  input  _4,
  input  _3,
  input  _2,
  input  _1,
  input  _0,
  input  _7_2,
  input  _6_2,
  input  _5_2,
  input  _4_2,
  input  in_15,
  input  _3_2,
  input  _2_2,
  input  _1_2,
  input  _0_2,
  output \串出 ,
  output _0_3,
  output _1_3,
  output _2_3,
  output _3_3,
  output _4_3,
  output _5_3,
  output \并出 ,
  output _7_3,
  output _7_4,
  output _6_3,
  output _5_4,
  output _4_4,
  output _3_4,
  output _2_4,
  output \并出_2 ,
  output _0_4,
  output \串出_2 
);

  wire clock_1_out, clock_2_out, clock_3_out, clock_4_out, main_5_qd;

  Clock clock_1 (.out(clock_1_out));
  Clock clock_2 (.out(clock_2_out));
  Clock clock_3 (.out(clock_3_out));
  _74x194_main main_1 (
    .CLK(clock_1_out), .CLR_L(1'b1), .S1(1'b0), .S0(1'b1), .LIN(1'b0), .D(1'b0), .C(1'b0), .B(1'b0),
    .A(1'b0), .RIN(\串入 ), .QA(\串出 ));  // open: QD, QC, QB
  _74x194_main main_2 (
    .CLK(clock_2_out), .CLR_L(1'b1), .S1(1'b0), .S0(1'b1), .LIN(1'b0), .D(1'b0), .C(1'b0), .B(1'b0),
    .A(1'b0), .RIN(\串入_2 ), .QD(_3_3), .QC(_2_3), .QB(_1_3), .QA(_0_3));
  _74x194_main main_3 (
    .CLK(clock_2_out), .CLR_L(1'b1), .S1(1'b0), .S0(1'b1), .LIN(1'b0), .D(1'b0), .C(1'b0), .B(1'b0),
    .A(1'b0), .RIN(_3_3), .QD(_7_3), .QC(\并出 ), .QB(_5_3), .QA(_4_3));
  _74x194_main main_4 (
    .CLK(clock_3_out), .CLR_L(1'b1), .S1(_7_2), .S0(1'b1), .LIN(1'b0), .D(_6_2), .C(_5_2), .B(_4_2),
    .A(in_15), .RIN(main_5_qd), .QD(\串出_2 ));  // open: QC, QB, QA
  _74x194_main main_5 (
    .CLK(clock_3_out), .CLR_L(1'b1), .S1(_7_2), .S0(1'b1), .LIN(1'b0), .D(_3_2), .C(_2_2), .B(_1_2),
    .A(_0_2), .RIN(1'b0), .QD(main_5_qd));  // open: QC, QB, QA
  Clock clock_4 (.out(clock_4_out));
  _74x194_main main_6 (
    .CLK(clock_4_out), .CLR_L(1'b1), .S1(1'b1), .S0(1'b1), .LIN(1'b0), .D(_7), .C(_6), .B(_5), .A(_4),
    .RIN(1'b0), .QD(_7_4), .QC(_6_3), .QB(_5_4), .QA(_4_4));
  _74x194_main main_7 (
    .CLK(clock_4_out), .CLR_L(1'b1), .S1(1'b1), .S0(1'b1), .LIN(1'b0), .D(_3), .C(_2), .B(_1), .A(_0),
    .RIN(1'b0), .QD(_3_4), .QC(_2_4), .QB(\并出_2 ), .QA(_0_4));

  // Notes on the sheet:
  //   switch
  //   并入
  //   6
  //   并入
  //   1
endmodule
