// Logisim project 自启动4位扭环计数器.circ as structural Verilog: 1 circuit, main circuit main
module main (
  output QD,
  output QC,
  output QB,
  output QA
);

  wire clock_1_out, nand_1_out, nand_2_out, not_1_out;

  Clock clock_1 (.out(clock_1_out));
  _74x194_main main_1 (
    .CLK(clock_1_out), .CLR_L(1'b1), .S1(1'b1), .S0(1'b0), .LIN(nand_1_out), .D(1'b0), .C(1'b0), .B(1'b0),
    .A(1'b0), .RIN(1'b0), .QD(QD), .QC(QC), .QB(QB), .QA(QA));
  nand nand_1 (nand_1_out, nand_2_out, QA);
  nand nand_2 (nand_2_out, QD, not_1_out);
  not not_1 (not_1_out, QB);
endmodule
