// Logisim project PingPang.circ as structural Verilog: 1 circuit, main circuit main
module main (
  input  \右侧选手击球 ,
  input  \左侧选手击球 ,
  input  \裁判复位开关 ,
  output out_4,
  output out_5,
  output out_6,
  output out_7,
  output out_8,
  output out_9,
  output out_10,
  output out_11
);

  wire _00_out, _02_2_out, _02_out, clock_1_out, d_ff_1_q, d_ff_1_qn, d_ff_2_q, d_ff_2_qn, d_ff_3_q,
       d_ff_3_qn, nand_1_out, nand_2_out, nand_3_out, nand_4_out, nand_5_out, nand_6_out, nand_7_out,
       nand_8_out, nor_1_out, nor_2_out, nor_3_out, nor_4_out, not_1_out, not_2_out, not_3_out, not_4_out,
       not_5_out, not_6_out, not_7_out, not_8_out, not_9_out, not_10_out, not_11_out;
  wire [3:0] n74163_1_qa, n74163_2_qa, n74163_3_qa, n74163_4_qa;

  Clock clock_1 (.out(clock_1_out));
  not not_1 (not_1_out, _02_out);
  not not_2 (not_2_out, nor_1_out);
  nor _02 (_02_out, \裁判复位开关 , d_ff_1_q);
  nor nor_1 (nor_1_out, d_ff_1_qn, \裁判复位开关 );
  not not_3 (not_3_out, nor_2_out);
  not not_4 (not_4_out, nand_1_out);
  _74x194_main _194 (
    .CLK(clock_1_out), .CLR_L(not_4_out), .S1(not_1_out), .S0(not_2_out), .LIN(1'b0), .D(d_ff_1_q), .C(1'b0),
    .B(1'b0), .A(1'b0), .RIN(out_8), .QD(out_4), .QC(out_5), .QB(out_6), .QA(out_7));
  _74x194_main main_1 (
    .CLK(clock_1_out), .CLR_L(not_4_out), .S1(not_1_out), .S0(not_2_out), .LIN(out_7), .D(1'b0), .C(1'b0),
    .B(1'b0), .A(d_ff_1_qn), .RIN(1'b0), .QD(out_8), .QC(out_9), .QB(out_10), .QA(out_11));
  D_Flip_Flop d_ff_1 (.clk(not_3_out), .D(d_ff_1_qn), .Q(d_ff_1_q), .Qn(d_ff_1_qn));  // open: preset, en, reset
  nor nor_2 (nor_2_out, \裁判复位开关 , not_5_out);
  not not_5 (not_5_out, nor_3_out);
  nand nand_1 (nand_1_out, nand_2_out, nand_3_out);
  nor nor_3 (nor_3_out, d_ff_2_q, d_ff_3_q);
  nor nor_4 (nor_4_out, out_5, \左侧选手击球 );
  not not_6 (not_6_out, nor_4_out);
  not not_7 (not_7_out, clock_1_out);
  nor _02_2 (_02_2_out, out_10, \右侧选手击球 );
  not not_8 (not_8_out, _02_2_out);
  D_Flip_Flop d_ff_2 (.clk(not_6_out), .D(out_4), .Q(d_ff_2_q), .Qn(d_ff_2_qn), .preset(1'b0), .en(1'b1), .reset(1'b0));
  D_Flip_Flop d_ff_3 (
    .clk(not_8_out), .D(out_11), .Q(d_ff_3_q), .Qn(d_ff_3_qn), .preset(1'b0), .en(1'b1), .reset(1'b0));
  nand nand_2 (nand_2_out, out_11, d_ff_1_q, not_7_out, d_ff_3_qn);
  nand nand_3 (nand_3_out, out_4, d_ff_1_qn, not_7_out, d_ff_2_qn);
  not not_9 (not_9_out, _00_out);
  nand nand_4 (nand_4_out, _00_out, clock_1_out);
  nand nand_5 (nand_5_out, nand_4_out, nand_2_out);
  nand nand_6 (nand_6_out, nand_4_out, nand_3_out);
  _74163 u_74163_1 (
    .A(1'b0), .B(1'b0), .C(1'b0), .D(1'b0), .ENT(1'b1), .ENP(1'b1), .LD_L(1'b1), .CLR_L(not_9_out),
    .QA(n74163_1_qa[0]), .QB(n74163_1_qa[1]), .QC(n74163_1_qa[2]), .QD(n74163_1_qa[3]), .CLK(nand_5_out));  // open: RCO
  _74163 u_74163_2 (
    .A(1'b0), .B(1'b0), .C(1'b0), .D(1'b0), .ENT(1'b1), .ENP(1'b1), .LD_L(1'b1), .CLR_L(not_9_out),
    .QA(n74163_2_qa[0]), .QB(n74163_2_qa[1]), .QC(n74163_2_qa[2]), .QD(n74163_2_qa[3]), .CLK(nand_6_out));  // open: RCO
  not not_10 (not_10_out, nand_8_out);
  nand _00 (_00_out, nand_8_out, nand_7_out);
  _74163 u_74163_3 (
    .A(1'b0), .B(1'b0), .C(1'b0), .D(1'b0), .ENT(not_11_out), .ENP(not_11_out), .LD_L(1'b1), .CLR_L(1'b1),
    .QA(n74163_3_qa[0]), .QB(n74163_3_qa[1]), .QC(n74163_3_qa[2]), .QD(n74163_3_qa[3]), .CLK(clock_1_out));  // open: RCO
  _74163 u_74163_4 (
    .A(1'b0), .B(1'b0), .C(1'b0), .D(1'b0), .ENT(not_10_out), .ENP(not_10_out), .LD_L(1'b1), .CLR_L(1'b1),
    .QA(n74163_4_qa[0]), .QB(n74163_4_qa[1]), .QC(n74163_4_qa[2]), .QD(n74163_4_qa[3]), .CLK(clock_1_out));  // open: RCO
  Hex_Digit_Display hex_digit_display_1 (.value(n74163_1_qa));  // open: dp
  nand nand_7 (nand_7_out, n74163_1_qa[3], n74163_1_qa[1], n74163_1_qa[0]);
  Hex_Digit_Display hex_digit_display_2 (.value(n74163_2_qa));  // open: dp
  nand nand_8 (nand_8_out, n74163_2_qa[3], n74163_2_qa[1], n74163_2_qa[0]);
  not not_11 (not_11_out, nand_7_out);
  Hex_Digit_Display hex_digit_display_3 (.value(n74163_3_qa));  // open: dp
  Hex_Digit_Display hex_digit_display_4 (.value(n74163_4_qa));  // open: dp

  // Notes on the sheet:
  //   时钟信号
  //   04
  //   04
  //   02
  //   04
  //   194
  //   04
  //   02
  //   02
  //   02
  //   04
  //   00
  //   04
  //   04
  //   04
  //   00
  //   20
  //   20
  //   04
  //   00
  //   00
  //   163
  //   163
  //   10
  //   10
  //   04
  //   左侧选手当前局内分数
  //   右侧选手当前局内分数
  //   左侧选手获胜局数
  //   04
  //   右侧选手获胜局数
endmodule
